# Fritzing sketch crayon-sonore (saved by Fritzing 0.9.3b)
breadboards: 1

parts:
  J1 = Piezo Speaker
  R1 = Resistor [tolerance=±5% resistance=10k package=THT]
  Part1 = Arduino Uno (Rev3)

nets:
  N1: J1.pin1, Part1.GND
  N2: J1.pin2, Part1.D9_PWM
  N3: R1.Pin_0, Part1.5V
  N4: R1.Pin_1, Part1.A0
